# Fritzing sketch ubicomp circuit (saved by Fritzing 0.9.3b)

parts:
  IC1 = AD8232 HeartRate Monitor [part_number=SEN-12650 chip_label=IC package="DIP (Dual Inline) [THT]"]
  Part1 = Arduino MKR1000

nets:
  GND: IC1.GND, Part1.GND
  3.3V: IC1.3.3v, Part1.VCC
  N1: IC1.OUTPUT, Part1.A1
  N2: IC1.LO-, Part1.D2_PWM
  N3: IC1.LO+, Part1.D1

custom parts:
  AD8232 HeartRate Monitor: A DIP stand-in part for whatever IC you want. With 10 pins on a 600mil dual inline package (DIP) footprint.
  Arduino MKR1000: MKR1000 is a powerful board that combines the functionality of the Zero and the Wi-Fi Shield. It is the ideal solution for makers wanting to design IoT projects with minimal previous experience in networking
